// Logisim project TallerLogicaSecuencialesVersionFinal.circ as structural Verilog: 17 circuits, main circuit registro_salida_restringida
module buffer_tres_estados (
  input  A,
  input  A_en,
  input  B,
  input  B_en,
  input  C,
  input  C_en,
  output Res
);

  assign Res = A_en ? A : 1'bz;  // Controlled_Buffer controlled_buffer_1
  assign Res = B_en ? B : 1'bz;  // Controlled_Buffer controlled_buffer_2
  assign Res = C_en ? C : 1'bz;  // Controlled_Buffer controlled_buffer_3
endmodule

module registro_salida_restringida (
  input  w,
  input  Reg_in,
  input  clk,
  input  en_out,
  output Reg_Debug,
  output Reg_output
);

  wire controlled_buffer_1_out;

  assign controlled_buffer_1_out = w ? Reg_in : 1'bz;  // Controlled_Buffer controlled_buffer_1
  D_Flip_Flop d_ff_1 (.D(controlled_buffer_1_out), .clk(clk), .Q(Reg_Debug));  // open: Qn, preset, reset
  assign Reg_output = en_out ? Reg_Debug : 1'bz;  // Controlled_Buffer controlled_buffer_2
endmodule

module registro_4bytes_salida (
  input  [3:0] Reg4_in,
  input  clk,
  input  w,
  input  en_out,
  output [3:0] Reg4_Debug,
  output [3:0] Reg4_output
);

  registro_salida_restringida registro_salida_restringida_1 (
    .Reg_in(Reg4_in[0]), .clk(clk), .w(w), .en_out(en_out), .Reg_Debug(Reg4_Debug[0]),
    .Reg_output(Reg4_output[0]));
  registro_salida_restringida registro_salida_restringida_2 (
    .Reg_in(Reg4_in[1]), .clk(clk), .w(w), .en_out(en_out), .Reg_Debug(Reg4_Debug[1]),
    .Reg_output(Reg4_output[1]));
  registro_salida_restringida registro_salida_restringida_3 (
    .Reg_in(Reg4_in[2]), .clk(clk), .w(w), .en_out(en_out), .Reg_Debug(Reg4_Debug[2]),
    .Reg_output(Reg4_output[2]));
  registro_salida_restringida registro_salida_restringida_4 (
    .Reg_in(Reg4_in[3]), .clk(clk), .w(w), .en_out(en_out), .Reg_Debug(Reg4_Debug[3]),
    .Reg_output(Reg4_output[3]));
endmodule

module ALU_regs (
  input  clk,
  input  [3:0] A,
  input  A_Write,
  input  [3:0] B,
  input  B_Write,
  input  S_En_Out,
  input  [1:0] OP,
  output [3:0] A_Debug,
  output [3:0] B_Debug,
  output N,
  output Z,
  output V,
  output C,
  output [3:0] S_Debug,
  output [3:0] Reg4_output
);

  wire not_1_out;
  wire [3:0] alu_1_s, registro_4bytes_salida_1_reg4_output, registro_4bytes_salida_2_reg4_output;

  Hex_Digit_Display hex_digit_display_1 (.value(A_Debug));  // open: dp
  registro_4bytes_salida registro_4bytes_salida_1 (
    .Reg4_in(A), .clk(clk), .w(A_Write), .en_out(1'b1), .Reg4_Debug(A_Debug),
    .Reg4_output(registro_4bytes_salida_1_reg4_output));
  registro_4bytes_salida registro_4bytes_salida_2 (
    .Reg4_in(B), .clk(clk), .w(B_Write), .en_out(1'b1), .Reg4_Debug(B_Debug),
    .Reg4_output(registro_4bytes_salida_2_reg4_output));
  Hex_Digit_Display hex_digit_display_2 (.value(B_Debug));  // open: dp
  not not_1 (not_1_out, clk);
  ALU alu_1 (
    .A(registro_4bytes_salida_1_reg4_output), .B(registro_4bytes_salida_2_reg4_output), .OP(OP), .N(N),
    .Z(Z), .V(V), .C(C), .S(alu_1_s));
  registro_4bytes_salida registro_4bytes_salida_3 (
    .Reg4_in(alu_1_s), .clk(not_1_out), .w(1'b1), .en_out(S_En_Out), .Reg4_Debug(S_Debug),
    .Reg4_output(Reg4_output));
  Hex_Digit_Display hex_digit_display_3 (.value(S_Debug));  // open: dp
endmodule

module ej_02 (
  input  w0,
  input  en_out0,
  input  w1,
  input  en_out1,
  input  clk,
  input  Force_Input,
  input  w2,
  input  en_out2,
  input  en_Force_Input,
  output R0,
  output E_S,
  output R1,
  output R2
);

  assign E_S = en_Force_Input ? Force_Input : 1'bz;  // Controlled_Buffer controlled_buffer_1
  registro_salida_restringida registro_salida_restringida_1 (
    .Reg_in(E_S), .clk(clk), .w(w0), .en_out(en_out0), .Reg_Debug(R0), .Reg_output(E_S));
  registro_salida_restringida registro_salida_restringida_2 (
    .Reg_in(E_S), .clk(clk), .w(w1), .en_out(en_out1), .Reg_Debug(R1), .Reg_output(E_S));
  registro_salida_restringida registro_salida_restringida_3 (
    .Reg_in(E_S), .clk(clk), .w(w2), .en_out(en_out2), .Reg_Debug(R2), .Reg_output(E_S));
endmodule

module ej_03 (
  input  clk,
  input  ALU_A_Write,
  input  ALU_B_Write,
  input  [1:0] OP,
  input  ALU_enableOut,
  input  Reg0_Write,
  input  Reg0_enableOut,
  input  Reg1_Write,
  input  Reg1_enableOut,
  input  Reg2_Write,
  input  Reg2_enableOut,
  input  Reg3_Write,
  input  Reg3_enableOut,
  input  [3:0] Force_Input,
  input  en_Force_Input,
  output N,
  output Z,
  output V,
  output C
);

  wire [3:0] alu_regs_1_a_debug, alu_regs_1_b_debug, alu_regs_1_s_debug, controlled_buffer_1_out,
       Registro_00_reg4_debug, Registro_00_reg4_output, Registro_01_reg4_debug, Registro_02_reg4_debug,
       Registro_03_reg4_debug;

  assign controlled_buffer_1_out = en_Force_Input ? Force_Input : 4'bz;  // Controlled_Buffer controlled_buffer_1
  registro_4bytes_salida Registro_00 (
    .Reg4_in(controlled_buffer_1_out), .clk(clk), .w(Reg0_Write), .en_out(Reg0_enableOut),
    .Reg4_Debug(Registro_00_reg4_debug), .Reg4_output(Registro_00_reg4_output));
  registro_4bytes_salida Registro_01 (
    .Reg4_in(controlled_buffer_1_out), .clk(clk), .w(Reg1_Write), .en_out(Reg1_enableOut),
    .Reg4_Debug(Registro_01_reg4_debug), .Reg4_output(Registro_00_reg4_output));
  registro_4bytes_salida Registro_02 (
    .Reg4_in(controlled_buffer_1_out), .clk(clk), .w(Reg2_Write), .en_out(Reg2_enableOut),
    .Reg4_Debug(Registro_02_reg4_debug), .Reg4_output(Registro_00_reg4_output));
  registro_4bytes_salida Registro_03 (
    .Reg4_in(controlled_buffer_1_out), .clk(clk), .w(Reg3_Write), .en_out(Reg3_enableOut),
    .Reg4_Debug(Registro_03_reg4_debug), .Reg4_output(Registro_00_reg4_output));
  Hex_Digit_Display hex_digit_display_1 (.value(Registro_00_reg4_debug));  // open: dp
  Hex_Digit_Display hex_digit_display_2 (.value(Registro_01_reg4_debug));  // open: dp
  Hex_Digit_Display hex_digit_display_3 (.value(Registro_02_reg4_debug));  // open: dp
  Hex_Digit_Display hex_digit_display_4 (.value(Registro_03_reg4_debug));  // open: dp
  Hex_Digit_Display hex_digit_display_5 (.value(alu_regs_1_a_debug));  // open: dp
  Hex_Digit_Display hex_digit_display_6 (.value(controlled_buffer_1_out));  // open: dp
  Hex_Digit_Display hex_digit_display_7 (.value(alu_regs_1_b_debug));  // open: dp
  ALU_regs alu_regs_1 (
    .A(Registro_00_reg4_output), .A_Write(ALU_A_Write), .B(Registro_00_reg4_output), .B_Write(ALU_B_Write),
    .clk(clk), .OP(OP), .S_En_Out(ALU_enableOut), .S_Debug(alu_regs_1_s_debug),
    .Reg4_output(controlled_buffer_1_out), .A_Debug(alu_regs_1_a_debug), .B_Debug(alu_regs_1_b_debug), .N(N),
    .Z(Z), .V(V), .C(C));
  Hex_Digit_Display hex_digit_display_8 (.value(alu_regs_1_s_debug));  // open: dp
endmodule

module sumador_simple (
  input  A,
  input  B,
  output S,
  output Cout
);

  xor xor_1 (S, A, B);
  and and_1 (Cout, A, B);
endmodule

module sumador_completo (
  input  Cin,
  input  A,
  input  B,
  output S,
  output Cout
);

  wire sumador_simple_1_cout, sumador_simple_1_s, sumador_simple_2_cout;

  sumador_simple sumador_simple_1 (.A(A), .B(B), .S(sumador_simple_1_s), .Cout(sumador_simple_1_cout));
  sumador_simple sumador_simple_2 (.A(sumador_simple_1_s), .B(Cin), .S(S), .Cout(sumador_simple_2_cout));
  or or_1 (Cout, sumador_simple_2_cout, sumador_simple_1_cout);
endmodule

module sumador_4 (
  input  Cin,
  input  [3:0] A,
  input  [3:0] B,
  output [3:0] S,
  output Cout
);

  wire sumador_completo_1_cout, sumador_completo_2_cout, sumador_completo_3_cout;

  sumador_completo sumador_completo_1 (.Cin(Cin), .A(A[0]), .B(B[0]), .S(S[0]), .Cout(sumador_completo_1_cout));
  sumador_completo sumador_completo_2 (
    .Cin(sumador_completo_1_cout), .A(A[1]), .B(B[1]), .S(S[1]), .Cout(sumador_completo_2_cout));
  sumador_completo sumador_completo_3 (
    .Cin(sumador_completo_2_cout), .A(A[2]), .B(B[2]), .S(S[2]), .Cout(sumador_completo_3_cout));
  sumador_completo sumador_completo_4 (.Cin(sumador_completo_3_cout), .A(A[3]), .B(B[3]), .S(S[3]), .Cout(Cout));
  Hex_Digit_Display hex_digit_display_1 (.value(S));  // open: dp
endmodule

module comparador_cero (
  input  [3:0] A,
  output Z
);

  wire or_1_out, or_2_out, or_3_out;

  or or_1 (or_1_out, A[0], A[1]);
  or or_2 (or_2_out, A[2], A[3]);
  or or_3 (or_3_out, or_1_out, or_2_out);
  not not_1 (Z, or_3_out);
endmodule

module sumador_flags (
  input  Cin,
  input  [3:0] A,
  input  [3:0] B,
  output [3:0] S,
  output N,
  output Z,
  output V,
  output C
);

  sumador_4 sumador_4_1 (.Cin(Cin), .A(A), .B(B), .S({N, S[2:0]}), .Cout(C));
  Hex_Digit_Display hex_digit_display_1 (.value({N, S[2:0]}));  // open: dp
  comparador_cero comparador_cero_1 (.A({N, S[2:0]}), .Z(Z));
  comp_overflow comp_overflow_1 (.c3(N), .a3(B[3]), .b3(A[3]), .O(V));

  assign S[3] = N;
endmodule

module incrementador_4 (
  input  [3:0] A,
  output [3:0] S
);

  sumador_4 sumador_4_1 (.A(A), .B(4'b0001), .S(S));  // open: Cin, Cout
  Hex_Digit_Display hex_digit_display_1 (.value(S));  // open: dp
endmodule

module inversor_4 (
  input  [3:0] A,
  input  INV,
  output [3:0] S
);

  wire [3:0] incrementador_4_1_s, not_1_out;

  not not_1 (not_1_out[0], A[0]);
  not not_2 (not_1_out[1], A[1]);
  not not_3 (not_1_out[2], A[2]);
  not not_4 (not_1_out[3], A[3]);
  Multiplexer #(.width(4)) multiplexer_1 (.in0(A), .in1(incrementador_4_1_s), .out(S), .sel(INV));
  incrementador_4 incrementador_4_1 (.A(not_1_out), .S(incrementador_4_1_s));
  Hex_Digit_Display hex_digit_display_1 (.value(S));  // open: dp
endmodule

module ALU (
  input  [3:0] A,
  input  [3:0] B,
  input  [1:0] OP,
  output N,
  output Z,
  output V,
  output C,
  output [3:0] S
);

  wire and_2_out, comparador_cero_1_z, overflow_resta_1_v_out, sumador_flags_1_c, sumador_flags_1_v;
  wire [3:0] and_1_out, inversor_4_1_s, or_1_out, sumador_flags_1_s;

  comparador_cero comparador_cero_1 (.A(B), .Z(comparador_cero_1_z));
  assign and_1_out = A & B;  // AND_Gate and_1, 4 bits wide
  assign or_1_out = A | B;  // OR_Gate or_1, 4 bits wide
  inversor_4 inversor_4_1 (.A(B), .INV(OP[0]), .S(inversor_4_1_s));
  sumador_flags sumador_flags_1 (
    .Cin(1'b0), .A(A), .B(inversor_4_1_s), .S(sumador_flags_1_s), .V(sumador_flags_1_v), .C(sumador_flags_1_c));  // open: N, Z
  Multiplexer #(.select(2), .width(4)) multiplexer_1 (
    .in0(sumador_flags_1_s), .in1(sumador_flags_1_s), .in2(and_1_out), .in3(or_1_out), .out({N, S[2:0]}),
    .sel(OP));
  overflow_resta overflow_resta_1 (.V_in(sumador_flags_1_v), .B(B), .V_out(overflow_resta_1_v_out));
  and and_2 (and_2_out, ~sumador_flags_1_c, ~comparador_cero_1_z);  // AND_Gate
  Multiplexer #(.select(2)) multiplexer_2 (
    .in0(sumador_flags_1_v), .in1(overflow_resta_1_v_out), .in2(1'b0), .in3(1'b0), .out(V), .sel(OP));
  Multiplexer #(.select(2)) multiplexer_3 (
    .in0(sumador_flags_1_c), .in1(and_2_out), .in2(1'b0), .in3(1'b0), .out(C), .sel(OP));
  Hex_Digit_Display hex_digit_display_1 (.value({N, S[2:0]}));  // open: dp
  comparador_cero comparador_cero_2 (.A({N, S[2:0]}), .Z(Z));

  assign S[3] = N;
endmodule

module verificador (
  output [3:0] out_1,
  output [3:0] out_2,
  output [1:0] out_3,
  output halt,
  output N,
  output Z,
  output V,
  output C,
  output [3:0] res
);

  wire clock_1_out;

  Clock clock_1 (.out(clock_1_out));
  Counter #(.max('h3ff), .width(10)) counter_1 (
    .clk(clock_1_out), .carry(halt), .Q({out_3, out_2, out_1}));  // open: clr, load, up, count, D
  ALU alu_1 (.A(out_1), .B(out_2), .OP(out_3), .N(N), .Z(Z), .V(V), .C(C), .S(res));
endmodule

module overflow_resta (
  input  V_in,
  input  [3:0] B,
  output V_out
);

  wire comparador_cero_1_z, not_2_out;
  wire [3:3] not_1_out;

  not not_1 (not_1_out[3], B[3]);
  not not_2 (not_2_out, V_in);
  comparador_cero comparador_cero_1 (.A({not_1_out[3], B[2:0]}), .Z(comparador_cero_1_z));
  Multiplexer multiplexer_1 (.in0(V_in), .in1(not_2_out), .out(V_out), .sel(comparador_cero_1_z));
endmodule

module comp_overflow (
  input  c3,
  input  a3,
  input  b3,
  output O
);

  wire not_1_out, xor_1_out, xor_2_out;

  xor xor_1 (xor_1_out, c3, a3);
  not not_1 (not_1_out, xor_2_out);
  xor xor_2 (xor_2_out, a3, b3);
  and and_1 (O, xor_1_out, not_1_out);
endmodule
