// Logisim project TallerLogica-Combinatorios.circ as structural Verilog: 10 circuits, main circuit verificador
module sumador_simple (
  input  A,
  input  B,
  output S,
  output Cout
);

  xor xor_1 (S, A, B);
  and and_1 (Cout, A, B);
endmodule

module sumador_completo (
  input  Cin,
  input  A,
  input  B,
  output S,
  output Cout
);

  wire sumador_simple_1_cout, sumador_simple_2_cout, sumador_simple_2_s;

  sumador_simple sumador_simple_1 (.A(Cin), .B(sumador_simple_2_s), .S(S), .Cout(sumador_simple_1_cout));
  sumador_simple sumador_simple_2 (.A(A), .B(B), .S(sumador_simple_2_s), .Cout(sumador_simple_2_cout));
  or or_1 (Cout, sumador_simple_1_cout, sumador_simple_2_cout);
endmodule

module sumador_4 (
  input  Cin,
  input  [3:0] A,
  input  [3:0] B,
  output [3:0] S,
  output Cout
);

  wire sumador_completo_1_cout, sumador_completo_2_cout, sumador_completo_3_cout;

  sumador_completo sumador_completo_1 (.A(A[0]), .B(B[0]), .Cin(Cin), .S(S[0]), .Cout(sumador_completo_1_cout));
  sumador_completo sumador_completo_2 (
    .A(A[1]), .B(B[1]), .Cin(sumador_completo_1_cout), .S(S[1]), .Cout(sumador_completo_2_cout));
  sumador_completo sumador_completo_3 (
    .A(A[2]), .B(B[2]), .Cin(sumador_completo_2_cout), .S(S[2]), .Cout(sumador_completo_3_cout));
  sumador_completo sumador_completo_4 (.A(A[3]), .B(B[3]), .Cin(sumador_completo_3_cout), .S(S[3]), .Cout(Cout));
  Hex_Digit_Display hex_digit_display_1 (.value(S));  // open: dp
endmodule

module comparador_cero (
  input  [3:0] A,
  output Z
);

  wire or_1_out, or_2_out, or_3_out;

  or or_1 (or_1_out, A[0], A[1]);
  or or_2 (or_2_out, A[2], A[3]);
  or or_3 (or_3_out, or_1_out, or_2_out);
  not not_1 (Z, or_3_out);
endmodule

module sumador_flags (
  input  Cin,
  input  [3:0] A,
  input  [3:0] B,
  output [3:0] S,
  output N,
  output Z,
  output V,
  output C
);

  wire xnor_1_out, xor_1_out;

  sumador_4 sumador_4_1 (.A(A), .B(B), .Cin(Cin), .Cout(C), .S({N, S[2:0]}));
  xnor xnor_1 (xnor_1_out, A[3], B[3]);
  xor xor_1 (xor_1_out, N, B[3]);
  Hex_Digit_Display hex_digit_display_1 (.value({N, S[2:0]}));  // open: dp
  and and_1 (V, xnor_1_out, xor_1_out);
  comparador_cero comparador_cero_1 (.A({N, S[2:0]}), .Z(Z));

  assign S[3] = N;
endmodule

module incrementador_4 (
  input  [3:0] A,
  output [3:0] S
);

  wire sumador_4_1_p3;
  wire [3:3] sumador_4_1_p2;

  // sumador_4 sumador_4_1: pin names not known; wires that end beside it: A, {4{sumador_4_1_p2[3]}}, sumador_4_1_p3, 1'b1, sumador_4_1_p3, S
  not not_1 (sumador_4_1_p2[3], 1'b1);
  Hex_Digit_Display hex_digit_display_1 (.value(S));  // open: dp
endmodule

module inversor_4 (
  input  [3:0] A,
  input  INV,
  output [3:0] S
);

  wire [3:0] incrementador_4_1_s, not_1_out;

  Multiplexer multiplexer_1 (.in0(A[0]), .in1(incrementador_4_1_s[0]), .out(S[0]), .sel(INV));
  not not_1 (not_1_out[0], A[0]);
  not not_2 (not_1_out[1], A[1]);
  not not_3 (not_1_out[2], A[2]);
  not not_4 (not_1_out[3], A[3]);
  Multiplexer multiplexer_2 (.in0(A[1]), .in1(incrementador_4_1_s[1]), .out(S[1]), .sel(INV));
  incrementador_4 incrementador_4_1 (.A(not_1_out), .S(incrementador_4_1_s));
  Multiplexer multiplexer_3 (.in0(A[2]), .in1(incrementador_4_1_s[2]), .out(S[2]), .sel(INV));
  Multiplexer multiplexer_4 (.in0(A[3]), .in1(incrementador_4_1_s[3]), .out(S[3]), .sel(INV));
endmodule

module verificador (
  output [3:0] out_1,
  output [3:0] out_2,
  output [1:0] out_3,
  output halt,
  output N,
  output Z,
  output V,
  output C,
  output [3:0] res
);

  wire clock_1_out;

  Clock clock_1 (.out(clock_1_out));
  Counter #(.max('h3ff), .width(10)) counter_1 (
    .clk(clock_1_out), .carry(halt), .Q({out_3, out_2, out_1}));  // open: clr, load, up, count, D
  ALU alu_1 (.A(out_1), .B(out_2), .OP(out_3), .N(N), .Z(Z), .V(V), .C(C), .S(res));
endmodule

module borrow (
  input  [3:0] A,
  input  [3:0] B,
  output borrow
);

  wire multiplexer_1_out, multiplexer_2_out, multiplexer_3_out, not_1_out, xor_1_out, xor_2_out, xor_3_out,
       xor_4_out;

  xor xor_1 (xor_1_out, B[0], A[0]);
  not not_1 (not_1_out, 1'b1);
  xor xor_2 (xor_2_out, B[1], A[1]);
  Multiplexer multiplexer_1 (.in0(multiplexer_2_out), .in1(B[1]), .out(multiplexer_1_out), .sel(xor_2_out));
  xor xor_3 (xor_3_out, A[3], B[3]);
  xor xor_4 (xor_4_out, A[2], B[2]);
  Multiplexer multiplexer_2 (.in0(not_1_out), .in1(B[0]), .out(multiplexer_2_out), .sel(xor_1_out));
  Multiplexer multiplexer_3 (.in0(multiplexer_1_out), .in1(B[2]), .out(multiplexer_3_out), .sel(xor_4_out));
  Multiplexer multiplexer_4 (.in0(multiplexer_3_out), .in1(B[3]), .out(borrow), .sel(xor_3_out));
endmodule

module ALU (
  input  [3:0] A,
  input  [3:0] B,
  input  [1:0] OP,
  output N,
  output Z,
  output V,
  output C,
  output [3:0] S
);

  wire [1:1] comparador_cero_2_z;
  wire [3:0] and_1_out, inversor_4_1_p3, or_1_out, sumador_flags_1_n, sumador_flags_1_s, sumador_flags_2_n,
       sumador_flags_2_s;
  wire [3:1] comparador_cero_1_z;

  // inversor_4 inversor_4_1: pin names not known; wires that end beside it: B, 1'b1, inversor_4_1_p3
  sumador_flags sumador_flags_1 (
    .A(A), .B(inversor_4_1_p3), .S(sumador_flags_1_s), .N(sumador_flags_1_n[0]), .Z(sumador_flags_1_n[1]),
    .V(sumador_flags_1_n[2]));  // open: Cin, C
  borrow borrow_1 (.A(A), .B(B), .borrow(sumador_flags_1_n[3]));
  and and_1 (and_1_out[0], A[0], B[0]);
  and and_2 (and_1_out[1], A[1], B[1]);
  and and_3 (and_1_out[2], A[2], B[2]);
  and and_4 (and_1_out[3], A[3], B[3]);
  or or_1 (or_1_out[0], A[0], B[0]);
  or or_2 (or_1_out[1], A[1], B[1]);
  or or_3 (or_1_out[2], A[2], B[2]);
  or or_4 (or_1_out[3], A[3], B[3]);
  comparador_cero comparador_cero_1 (.A(and_1_out), .Z(comparador_cero_1_z[1]));
  sumador_flags sumador_flags_2 (
    .A(A), .B(B), .S(sumador_flags_2_s), .N(sumador_flags_2_n[0]), .Z(sumador_flags_2_n[1]),
    .V(sumador_flags_2_n[2]), .C(sumador_flags_2_n[3]));  // open: Cin
  Multiplexer #(.select(2), .width(4)) multiplexer_1 (
    .in0(sumador_flags_2_s), .in1(sumador_flags_1_s), .in2(and_1_out), .in3(or_1_out), .out(S), .sel(OP));
  not not_1 (comparador_cero_1_z[3], 1'b1);
  comparador_cero comparador_cero_2 (.A(or_1_out), .Z(comparador_cero_2_z[1]));
  Hex_Digit_Display hex_digit_display_1 (.value(S));  // open: dp
  Multiplexer #(.select(2), .width(4)) multiplexer_2 (
    .in0(sumador_flags_2_n), .in1(sumador_flags_1_n),
    .in2({{2{comparador_cero_1_z[3]}}, comparador_cero_1_z[1], and_1_out[3]}),
    .in3({{2{comparador_cero_1_z[3]}}, comparador_cero_2_z[1], or_1_out[3]}), .out({C, V, Z, N}), .sel(OP));
endmodule
